# Fritzing sketch pirrigation (saved by Fritzing 0.9.3b)
breadboards: 1

parts:
  Q1 = NPN-Transistor [package="SOT-23 [SMD]"]
  D9358_-_pump = DC Motor
  Raspberry_Pi1 = Raspberry Pi B+
  D1 = Rectifier Diode [part_number=1N4001 package="300 mil [THT]"]
  R1 = Resistor [tolerance=±5% resistance=1k package=THT]
  R2 = Resistor [tolerance=±5% resistance=1k package=THT]
  Solenoid_Valve = Solenoid
  VCC1 = Battery block 9V

nets:
  N1: Q1.2, R2.Pin_0, VCC1.-
  N2: Q1.0, R1.Pin_0
  N3: Q1.1, D9358_-_pump.pin_2
  N4: D9358_-_pump.pin_1, Solenoid_Valve.pin1
  N5: Raspberry_Pi1.GPIO26, R1.Pin_1
  N6: Raspberry_Pi1.GND, R2.Pin_1
  N7: D1.anode, Solenoid_Valve.pin2, VCC1.+
